# Fritzing sketch wc (saved by Fritzing 0.9.3b)
circuit board: 6.62434cm x 3.06737cm
breadboards: 1

parts:
  TWE-Lite(DIP)1 = TWE-Lite DIP [package=DIP]
  R1 = Resistor [tolerance=±5% resistance=1M package=THT]
  Reed_SW = Reed switch [package=THT]
  BAT1 = Battery Holders [package=battcom_20mm_pth]

nets:
  N1: TWE-Lite(DIP)1.GND#0, R1.Pin_0, BAT1.-
  N2: TWE-Lite(DIP)1.AI_1, R1.Pin_1, Reed_SW.pin_2
  N3: TWE-Lite(DIP)1.VCC, Reed_SW.pin_1, BAT1.+

custom parts:
  TWE-Lite DIP: TWE-Lite for DIP. 28 pins.
